# Fritzing sketch Teensy DC motor driver_2 (saved by Fritzing 0.8.5b)
circuit board: 5.85727cm x 5.68102cm
breadboards: 1

parts:
  IC1 = H-Bridge [part_number=754410 package=THT]
  M1 = DC Motor [part_number="LHS motor"]
  M2 = DC Motor [part_number="RHS motor"]
  Teensy1 = Teensy 2.0
  S1 = Pushbutton [part_number=Start package="[THT]"]
  R1 = Resistor [tolerance=±5% resistance=150 package=THT]
  LED1 = LED - 5mm [color="Red (633nm)" package="5 mm [THT]"]
  R2 = Resistor [tolerance=±5% resistance=150 package=THT]
  LED2 = LED - 5mm [color="Red (633nm)" package="5 mm [THT]"]
  C1 = Ceramic Capacitor [capacitance=100nF package="100 mil [THT, multilayer]"]
  C2 = Ceramic Capacitor [capacitance=100nF package="100 mil [THT, multilayer]"]
  U1 = Voltage Regulator - 5V [package="TO220 [THT]"]
  J2 = Screw terminal - 2 pins [part_number="Motor power" package=THT]
  J3 = Screw terminal - 2 pins [part_number="Motor power" package=THT]
  J4 = Screw terminal - 2 pins [part_number="Motor power" package=THT]

nets:
  N1: IC1.1_2EN, Teensy1.C7
  N2: IC1.1A, Teensy1.B0
  N3: IC1.1Y, M1.pin_1, R1.Pin_0, R1.Pin_1, LED1.anode
  GND: IC1.GND1, IC1.GND2, IC1.GND3, IC1.GND4, Teensy1.GND, S1.Pin_3, S1.Pin_4, C1.1, C2.1, U1.GND, J2.pin1
  N4: IC1.2Y, M1.pin_2, LED1.cathode
  N5: IC1.2A, Teensy1.B1
  N6: IC1.VCC2, C2.0, U1.input_voltage, J2.pin2
  N7: IC1.3_4EN, Teensy1.D7
  N8: IC1.3A, Teensy1.B2
  N9: IC1.3Y, M2.pin_1, R2.Pin_0, R2.Pin_1, LED2.anode
  N10: IC1.4Y, M2.pin_2, LED2.cathode
  N11: IC1.4A, Teensy1.B3
  N12: IC1.VCC1, Teensy1.VCC, C1.0, U1.output_voltage
  N13: Teensy1.B7, J3.pin2
  N14: Teensy1.D0, J3.pin1
  N15: Teensy1.B4, S1.Pin_1, S1.Pin_2
  N16: Teensy1.B5, J4.pin2
  N17: Teensy1.B6, J4.pin1

notes:
  inner: +5V
  outer: Gnd
  outer: +5V
  inner: Gnd
  AA battery pack:
  5 (or 4) alkaline OR
  6 (or 5) NiMH rechargeable.
  If no 5V regulator, don't exceed 6.0 V open circuit !!
  See note on SCH view
  Battery pack:
  If no 5V regulator, don't exceed 6.0 V open circuit !!
  See note on BB view.
  Teensy recommends separating 5V supply from USB 5V (see https://www.pjrc.com/teensy/external_power.html). This requires either cutting a PCB trace or a wire in the USB cable.
  Motor LEDs optional. Useful if debugging using only USB power
  or battery voltage is too low to run motors.
  Wheel encoder A,B
